// Digital circuit pong.dig as structural Verilog
module pong (
  input  clk
);

  wire _1_out, _1_plus_out, _2_out, _2_plus_out, and_1_out, horizontal_fim, horizontal_mostra,
       horizontal_sinc, inicializa_out, jogador_1_p3, jogador_1_p8, jogador_1_p9, jogador_1_p10,
       jogador_1_p11, jogador_1_p12, jogador_1_p13, jogador_1_p14, jogador_1_p15, jogador_1_p16,
       jogador_1_p17, not_1_out, not_2_out, not_3_out, pintor_1_p11, pintor_1_p12, pintor_1_p13,
       pintor_1_p14, pintor_1_p15, pintor_1_p16, vertical_mostra;
  wire [2:0] priorityencoder_1_num;
  wire [11:0] horizontal_contagem, vertical_contagem;
  wire [23:0] multiplexer_1_out;

  Button inicializa (.out(inicializa_out));
  Button _1_plus (.out(_1_plus_out));
  Button _1 (.out(_1_out));
  Button _2_plus (.out(_2_plus_out));
  Button _2 (.out(_2_out));
  // jogador jogador_1: pin names not known; wires that end beside it: clk, inicializa_out, jogador_1_p3, _1_plus_out, _1_out, _2_plus_out, _2_out, jogador_1_p8, jogador_1_p9, jogador_1_p10, jogador_1_p11, jogador_1_p12, jogador_1_p13, jogador_1_p14, jogador_1_p15, jogador_1_p16, jogador_1_p17
  temporiza vertical (
    .relogio(clk), .conta(horizontal_fim), .inicializa(inicializa_out), .upix(12'h1df), .inisinc(12'h1e9),
    .fimsinc(12'h1eb), .fimcont(12'h20c), .contagem(vertical_contagem), .mostra(vertical_mostra),
    .sinc(jogador_1_p3));  // open: fim
  temporiza horizontal (
    .relogio(clk), .conta(1'b1), .inicializa(inicializa_out), .upix(12'h27f), .inisinc(12'h28f),
    .fimsinc(12'h2ef), .fimcont(12'h31f), .contagem(horizontal_contagem), .fim(horizontal_fim),
    .mostra(horizontal_mostra), .sinc(horizontal_sinc));
  // pintor pintor_1: pin names not known; wires that end beside it: horizontal_contagem, vertical_contagem, jogador_1_p10, jogador_1_p11, jogador_1_p12, jogador_1_p13, jogador_1_p14, jogador_1_p15, jogador_1_p16, jogador_1_p17, pintor_1_p11, pintor_1_p12, pintor_1_p13, pintor_1_p14, pintor_1_p15, pintor_1_p16
  not not_1 (not_1_out, jogador_1_p3);
  not not_2 (not_2_out, horizontal_sinc);
  and and_1 (and_1_out, vertical_mostra, horizontal_mostra);
  and and_2 (jogador_1_p8, pintor_1_p16, pintor_1_p15);
  and and_3 (jogador_1_p9, pintor_1_p16, pintor_1_p13);
  not not_3 (not_3_out, and_1_out);
  PriorityEncoder #(.Selector_Bits(3)) priorityencoder_1 (
    .in0(1'b1), .in1(pintor_1_p11), .in2(pintor_1_p12), .in3(pintor_1_p13), .in4(pintor_1_p14),
    .in5(pintor_1_p15), .in6(pintor_1_p16), .in7(not_3_out), .num(priorityencoder_1_num));  // open: any
  Multiplexer #(.Selector_Bits(3), .Bits(24)) multiplexer_1 (
    .sel(priorityencoder_1_num), .in_0(24'h8000), .in_1(24'hfff0ff), .in_2(24'hff7f00), .in_3(24'hff7f00),
    .in_4(24'h7fff), .in_5(24'h7fff), .in_6(24'hffff), .in_7({24{1'b0}}), .out(multiplexer_1_out));
  VGA vga_1 (
    .R(multiplexer_1_out[7:0]), .G(multiplexer_1_out[15:8]), .B(multiplexer_1_out[23:16]), .H(not_2_out),
    .V(not_1_out), .C(clk));

  // Notes on the sheet:
  //   clk: Hz: 2147483647
  //   640x480 60Hz, 25.175MHz, 640, 16, 96, 48, 480, 11, 2, 31
endmodule
